# Fritzing sketch luz_emergencia (saved by Fritzing 0.9.3b)
breadboards: 1

parts:
  Part1 = Tessel 2
  LED1 = LED - 5mm [color="Red (633nm)" package="5 mm [THT]"]
  R1 = Photocell (LDR) [package=THT]
  R2 = Resistor [tolerance=±5% resistance=330 package=THT]

nets:
  N1: Part1.GND, LED1.cathode, R2.Pin_1
  N2: Part1.3V3, R1.pin_1
  N3: Part1.0, LED1.anode
  N4: Part1.7, R1.pin_0, R2.Pin_0

custom parts:
  Tessel 2: Draft version of Tessel 2
